// Logisim project adder.circ as structural Verilog: 2 circuits, main circuit main
// sub
module main (
  input  sub,
  input  in_2,
  input  [15:0] B,
  input  [15:0] A,
  output ovf,
  output [15:0] result
);

  wire not_1_out, not_2_out, not_3_out, not_4_out, not_5_out, not_6_out, not_7_out, not_8_out, not_9_out,
       not_10_out, not_11_out, not_12_out, not_13_out, not_14_out, not_15_out, not_16_out,
       onebitadder_1_cout, onebitadder_1_sum, onebitadder_2_cout, onebitadder_2_sum, onebitadder_3_cout,
       onebitadder_3_sum, onebitadder_4_cout, onebitadder_4_sum, onebitadder_5_cout, onebitadder_5_sum,
       onebitadder_6_cout, onebitadder_6_sum, onebitadder_7_cout, onebitadder_7_sum, onebitadder_8_cout,
       onebitadder_8_sum, onebitadder_9_cout, onebitadder_9_sum, onebitadder_10_cout, onebitadder_10_sum,
       onebitadder_11_cout, onebitadder_11_sum, onebitadder_12_cout, onebitadder_12_sum, onebitadder_13_cout,
       onebitadder_13_sum, onebitadder_14_cout, onebitadder_14_sum, onebitadder_15_cout, onebitadder_15_sum,
       onebitadder_16_cout, onebitadder_16_sum, xor_1_out, xor_2_out, xor_4_out, xor_5_out, xor_6_out,
       xor_7_out, xor_8_out, xor_9_out, xor_10_out, xor_11_out, xor_12_out, xor_13_out, xor_14_out,
       xor_15_out, xor_16_out, xor_17_out;

  Multiplexer multiplexer_1 (.in0(onebitadder_1_sum), .in1(not_1_out), .out(result[7]), .sel(sub));  // open: en
  not not_1 (not_1_out, onebitadder_1_sum);
  onebitadder onebitadder_1 (
    .a(xor_1_out), .b(B[7]), .Sum(onebitadder_1_sum), .Cin(onebitadder_3_cout), .Cout(onebitadder_1_cout));
  xor xor_1 (xor_1_out, A[7], sub);
  Multiplexer multiplexer_2 (.in0(onebitadder_2_sum), .in1(not_2_out), .out(result[15]), .sel(sub));  // open: en
  not not_2 (not_2_out, onebitadder_2_sum);
  onebitadder onebitadder_2 (
    .a(xor_2_out), .b(B[15]), .Sum(onebitadder_2_sum), .Cin(onebitadder_4_cout), .Cout(onebitadder_2_cout));
  xor xor_2 (xor_2_out, A[15], sub);
  xor xor_3 (ovf, onebitadder_2_cout, onebitadder_4_cout);
  Multiplexer multiplexer_3 (.in0(onebitadder_3_sum), .in1(not_3_out), .out(result[6]), .sel(sub));  // open: en
  not not_3 (not_3_out, onebitadder_3_sum);
  onebitadder onebitadder_3 (
    .a(xor_4_out), .b(B[6]), .Sum(onebitadder_3_sum), .Cin(onebitadder_5_cout), .Cout(onebitadder_3_cout));
  xor xor_4 (xor_4_out, A[6], sub);
  Multiplexer multiplexer_4 (.in0(onebitadder_4_sum), .in1(not_4_out), .out(result[14]), .sel(sub));  // open: en
  not not_4 (not_4_out, onebitadder_4_sum);
  onebitadder onebitadder_4 (
    .a(xor_5_out), .b(B[14]), .Sum(onebitadder_4_sum), .Cin(onebitadder_6_cout), .Cout(onebitadder_4_cout));
  xor xor_5 (xor_5_out, A[14], sub);
  Multiplexer multiplexer_5 (.in0(onebitadder_5_sum), .in1(not_5_out), .out(result[5]), .sel(sub));  // open: en
  not not_5 (not_5_out, onebitadder_5_sum);
  onebitadder onebitadder_5 (
    .a(xor_6_out), .b(B[5]), .Sum(onebitadder_5_sum), .Cin(onebitadder_7_cout), .Cout(onebitadder_5_cout));
  xor xor_6 (xor_6_out, A[5], sub);
  Multiplexer multiplexer_6 (.in0(onebitadder_6_sum), .in1(not_6_out), .out(result[13]), .sel(sub));  // open: en
  not not_6 (not_6_out, onebitadder_6_sum);
  onebitadder onebitadder_6 (
    .a(xor_7_out), .b(B[13]), .Sum(onebitadder_6_sum), .Cin(onebitadder_8_cout), .Cout(onebitadder_6_cout));
  xor xor_7 (xor_7_out, A[13], sub);
  Multiplexer multiplexer_7 (.in0(onebitadder_7_sum), .in1(not_7_out), .out(result[4]), .sel(sub));  // open: en
  not not_7 (not_7_out, onebitadder_7_sum);
  onebitadder onebitadder_7 (
    .a(xor_8_out), .b(B[4]), .Sum(onebitadder_7_sum), .Cin(onebitadder_9_cout), .Cout(onebitadder_7_cout));
  xor xor_8 (xor_8_out, A[4], sub);
  Multiplexer multiplexer_8 (.in0(onebitadder_8_sum), .in1(not_8_out), .out(result[12]), .sel(sub));  // open: en
  not not_8 (not_8_out, onebitadder_8_sum);
  onebitadder onebitadder_8 (
    .a(xor_9_out), .b(B[12]), .Sum(onebitadder_8_sum), .Cin(onebitadder_10_cout), .Cout(onebitadder_8_cout));
  xor xor_9 (xor_9_out, A[12], sub);
  Multiplexer multiplexer_9 (.in0(onebitadder_9_sum), .in1(not_9_out), .out(result[3]), .sel(sub));  // open: en
  Multiplexer multiplexer_10 (.in0(onebitadder_11_sum), .in1(not_11_out), .out(result[2]), .sel(sub));  // open: en
  not not_9 (not_9_out, onebitadder_9_sum);
  onebitadder onebitadder_9 (
    .a(xor_10_out), .b(B[3]), .Sum(onebitadder_9_sum), .Cin(onebitadder_11_cout), .Cout(onebitadder_9_cout));
  xor xor_10 (xor_10_out, A[3], sub);
  Multiplexer multiplexer_11 (.in0(onebitadder_10_sum), .in1(not_10_out), .out(result[11]), .sel(sub));  // open: en
  not not_10 (not_10_out, onebitadder_10_sum);
  onebitadder onebitadder_10 (
    .a(xor_11_out), .b(B[11]), .Sum(onebitadder_10_sum), .Cin(onebitadder_12_cout), .Cout(onebitadder_10_cout));
  xor xor_11 (xor_11_out, A[11], sub);
  Multiplexer multiplexer_12 (.in0(onebitadder_13_sum), .in1(not_12_out), .out(result[1]), .sel(sub));  // open: en
  not not_11 (not_11_out, onebitadder_11_sum);
  not not_12 (not_12_out, onebitadder_13_sum);
  onebitadder onebitadder_11 (
    .a(xor_12_out), .b(B[2]), .Sum(onebitadder_11_sum), .Cin(onebitadder_13_cout), .Cout(onebitadder_11_cout));
  xor xor_12 (xor_12_out, A[2], sub);
  Multiplexer multiplexer_13 (.in0(onebitadder_14_sum), .in1(not_15_out), .out(result[9]), .sel(sub));  // open: en
  Multiplexer multiplexer_14 (.in0(onebitadder_12_sum), .in1(not_13_out), .out(result[10]), .sel(sub));  // open: en
  not not_13 (not_13_out, onebitadder_12_sum);
  onebitadder onebitadder_12 (
    .a(xor_13_out), .b(B[10]), .Sum(onebitadder_12_sum), .Cin(onebitadder_14_cout), .Cout(onebitadder_12_cout));
  xor xor_13 (xor_13_out, A[10], sub);
  Multiplexer multiplexer_15 (.in0(onebitadder_15_sum), .in1(not_14_out), .out(result[0]), .sel(sub));  // open: en
  not not_14 (not_14_out, onebitadder_15_sum);
  onebitadder onebitadder_13 (
    .a(xor_14_out), .b(B[1]), .Sum(onebitadder_13_sum), .Cin(onebitadder_15_cout), .Cout(onebitadder_13_cout));
  xor xor_14 (xor_14_out, A[1], sub);
  Multiplexer multiplexer_16 (.in0(onebitadder_16_sum), .in1(not_16_out), .out(result[8]), .sel(sub));  // open: en
  not not_15 (not_15_out, onebitadder_14_sum);
  onebitadder onebitadder_14 (
    .a(xor_15_out), .b(B[9]), .Sum(onebitadder_14_sum), .Cin(onebitadder_16_cout), .Cout(onebitadder_14_cout));
  xor xor_15 (xor_15_out, A[9], sub);
  onebitadder onebitadder_15 (
    .a(xor_16_out), .b(B[0]), .Sum(onebitadder_15_sum), .Cin(in_2), .Cout(onebitadder_15_cout));
  xor xor_16 (xor_16_out, A[0], sub);
  not not_16 (not_16_out, onebitadder_16_sum);
  onebitadder onebitadder_16 (
    .a(xor_17_out), .b(B[8]), .Sum(onebitadder_16_sum), .Cin(onebitadder_1_cout), .Cout(onebitadder_16_cout));
  xor xor_17 (xor_17_out, A[8], sub);

  // Other names for the same wires on the sheet: s0 = result[0]; s1 = result[1]; s2 = result[2]; s3 = result[3];
  //   s4 = result[4]; s5 = result[5]; s6 = result[6]; s7 = result[7]; s8 = result[8]; s9 = result[9];
  //   s10 = result[10]; s11 = result[11]; s12 = result[12]; s13 = result[13]; s14 = result[14]; s15 = result[15]
endmodule

module onebitadder (
  input  Cin,
  input  a,
  input  b,
  output Sum,
  output Cout
);

  wire and_1_out, and_2_out, xor_1_out;

  and and_1 (and_1_out, b, a);
  xor xor_1 (xor_1_out, a, b);
  or or_1 (Cout, and_1_out, and_2_out);
  and and_2 (and_2_out, xor_1_out, Cin);
  xor xor_2 (Sum, Cin, xor_1_out);
endmodule
